// Logisim project curcuit.circ as structural Verilog: 4 circuits, main circuit CPU
module CPU (
);

  wire ALU_carry, ALU_comp, ALU_out, and_1_out, cpu_clock, instruction_decoder_1_ir_in,
       instruction_decoder_1_ir_out, jump, num1_in, num1_out, num2_in, num2_out, PC_out, PC_up, RAM_adr_in,
       RAM_in, RAM_out;
  wire [3:0] ALU_inst, bit_extender_5_out;
  wire [15:0] bit_extender_1_out, bit_extender_2_out, programcounter_1_ip, programcounter_2_ip, register_1_q,
       register_2_q, register_2_q_2;
  wire [31:0] alu_1_num_out, ALU_out_q, bit_extender_3_out, bit_extender_4_out, multiplexer_1_out, num1_q,
       num2_q, ram_1_dout;

  RAM #(.addrWidth(16), .dataWidth(32)) ram_1 (
    .addr(register_1_q), .we(RAM_in), .oe(RAM_out), .clk(cpu_clock), .din(multiplexer_1_out),
    .dout(ram_1_dout));
  Clock #(.phaseOffset(1)) clock_1 (.out(cpu_clock));
  Register #(.width(16)) register_1 (
    .D(bit_extender_2_out), .en(RAM_adr_in), .clk(cpu_clock), .Q(register_1_q));  // open: clr
  Bit_Extender #(.in_width(32), .\type ("zero")) bit_extender_1 (.in(multiplexer_1_out), .out(bit_extender_1_out));
  Bit_Extender #(.in_width(32), .\type ("zero")) bit_extender_2 (.in(multiplexer_1_out), .out(bit_extender_2_out));
  ProgramCounter programcounter_1 (
    .JmpAddr(bit_extender_1_out), .Jmp(jump), .Clock(PC_up), .ip(programcounter_1_ip));  // open: Reset
  Multiplexer #(.width(32)) multiplexer_1 (
    .in1(bit_extender_3_out), .out(multiplexer_1_out), .sel(PC_out));  // open: in0
  assign bit_extender_3_out = {{16{programcounter_1_ip[15]}}, programcounter_1_ip};  // Bit_Extender bit_extender_3
  Multiplexer #(.width(32)) multiplexer_2 (.in1(ram_1_dout), .out(multiplexer_1_out), .sel(RAM_out));  // open: in0
  LedBar #(.matrixcols(32)) ledbar_1 (
    .led0(multiplexer_1_out[31]), .led1(multiplexer_1_out[30]), .led2(multiplexer_1_out[29]),
    .led3(multiplexer_1_out[28]), .led4(multiplexer_1_out[27]), .led5(multiplexer_1_out[26]),
    .led6(multiplexer_1_out[25]), .led7(multiplexer_1_out[24]), .led8(multiplexer_1_out[23]),
    .led9(multiplexer_1_out[22]), .led10(multiplexer_1_out[21]), .led11(multiplexer_1_out[20]),
    .led12(multiplexer_1_out[19]), .led13(multiplexer_1_out[18]), .led14(multiplexer_1_out[17]),
    .led15(multiplexer_1_out[16]), .led16(multiplexer_1_out[15]), .led17(multiplexer_1_out[14]),
    .led18(multiplexer_1_out[13]), .led19(multiplexer_1_out[12]), .led20(multiplexer_1_out[11]),
    .led21(multiplexer_1_out[10]), .led22(multiplexer_1_out[9]), .led23(multiplexer_1_out[8]),
    .led24(multiplexer_1_out[7]), .led25(multiplexer_1_out[6]), .led26(multiplexer_1_out[5]),
    .led27(multiplexer_1_out[4]), .led28(multiplexer_1_out[3]), .led29(multiplexer_1_out[2]),
    .led30(multiplexer_1_out[1]), .led31(multiplexer_1_out[0]));
  Multiplexer #(.width(32)) multiplexer_3 (
    .in1(bit_extender_4_out), .out(multiplexer_1_out), .sel(instruction_decoder_1_ir_out));  // open: in0
  Multiplexer #(.width(32)) multiplexer_4 (.in1(num1_q), .out(multiplexer_1_out), .sel(num1_out));  // open: in0
  Multiplexer #(.width(32)) multiplexer_5 (.in1(num2_q), .out(multiplexer_1_out), .sel(num2_out));  // open: in0
  Register #(.width(32)) register_2 (
    .D(multiplexer_1_out), .en(instruction_decoder_1_ir_in), .Q({register_2_q, register_2_q_2}));  // open: clk, clr
  assign bit_extender_4_out = {{16{1'b0}}, register_2_q};  // Bit_Extender bit_extender_4
  Register #(.width(32)) num1 (.D(multiplexer_1_out), .en(num1_in), .clk(cpu_clock), .Q(num1_q));  // open: clr
  Register #(.width(32)) num2 (.D(multiplexer_1_out), .en(num2_in), .clk(cpu_clock), .Q(num2_q));  // open: clr
  and and_1 (and_1_out, bit_extender_5_out[0], bit_extender_5_out[1], bit_extender_5_out[2], bit_extender_5_out[3]);
  ALU alu_1 (
    .instruction(ALU_inst), .num1(num1_q), .num2(num2_q), .carry_out(ALU_carry), .comp_out(ALU_comp),
    .num_out(alu_1_num_out));  // open: borrow_in, carry_in, mul_carry_in, div_upper, borrow_out
  Bit_Extender #(.in_width(16), .out_width(4)) bit_extender_5 (.in(programcounter_2_ip), .out(bit_extender_5_out));
  ProgramCounter programcounter_2 (
    .Reset(and_1_out), .Clock(cpu_clock), .ip(programcounter_2_ip));  // open: JmpAddr, Jmp
  instruction_decoder instruction_decoder_1 (
    .sub_stage(bit_extender_5_out), .instruction(register_2_q_2), .carry(ALU_carry), .comp(ALU_comp),
    .PC_out(PC_out), .jump(jump), .PC_up(PC_up), .RAM_adr_in(RAM_adr_in), .RAM_in(RAM_in), .RAM_out(RAM_out),
    .num1_out(num1_out), .num1_in(num1_in), .num2_out(num2_out), .num2_in(num2_in), .ALU_inst(ALU_inst),
    .ALU_out(ALU_out), .IR_in(instruction_decoder_1_ir_in), .IR_out(instruction_decoder_1_ir_out));
  Register #(.width(32)) u_ALU_out (.D(alu_1_num_out), .en(1'b1), .clk(cpu_clock), .Q(ALU_out_q));  // open: clr
  Multiplexer #(.width(32)) multiplexer_6 (.in1(ALU_out_q), .out(multiplexer_1_out), .sel(ALU_out));  // open: in0
endmodule

module ProgramCounter (
  input  [15:0] JmpAddr,
  input  Reset,
  input  Jmp,
  input  Clock,
  output [15:0] ip
);

  wire [15:0] adder_1_out, multiplexer_1_out;

  Adder #(.width(16)) adder_1 (.a(ip), .b(16'h1), .out(adder_1_out));  // open: cin, cout
  Multiplexer #(.width(16)) multiplexer_1 (.in0(adder_1_out), .in1(JmpAddr), .out(multiplexer_1_out), .sel(Jmp));
  Register #(.width(16)) register_1 (.D(multiplexer_1_out), .en(1'b1), .Q(ip), .clk(Clock), .clr(Reset));
endmodule

module ALU (
  input  [3:0] instruction,
  input  [31:0] num1,
  input  [31:0] num2,
  input  borrow_in,
  input  carry_in,
  input  [31:0] mul_carry_in,
  input  [31:0] div_upper,
  output carry_out,
  output borrow_out,
  output comp_out,
  output [31:0] num_out
);

  wire comparator_1_eq, comparator_1_gt, comparator_1_lt, comparator_2_eq, comparator_2_gt, comparator_2_lt,
       fpcomparator_1_p3, fpcomparator_1_p4, fpcomparator_1_p5, fpcomparator_2_p3, fpcomparator_2_p4,
       fpcomparator_2_p5;
  wire [31:0] adder_1_out, divider_1_out, divider_2_out, fpadder_1_out, fpdivider_1_out, fpmultiplier_1_out,
       fpnegator_1_p2, fpsubtractor_1_out, fptoint_1_p2, inttofp_1_p2, multiplier_1_out, multiplier_2_out,
       negator_1_out, subtractor_1_out;

  Adder #(.width(32)) adder_1 (.a(num2), .b(num1), .out(adder_1_out), .cin(carry_in), .cout(carry_out));
  Subtractor #(.width(32)) subtractor_1 (
    .a(num2), .b(num1), .out(subtractor_1_out), .bin(borrow_in), .bout(borrow_out));
  Multiplier #(.width(32)) multiplier_1 (.a(num2), .b(num1), .out(multiplier_1_out), .cin(mul_carry_in));  // open: cout
  Multiplier #(.mode("twosComplement"), .width(32)) multiplier_2 (
    .a(num2), .b(num1), .out(multiplier_2_out), .cin(mul_carry_in));  // open: cout
  Divider #(.width(32)) divider_1 (.a(num2), .b(num1), .out(divider_1_out), .upper(div_upper));  // open: rem
  Divider #(.mode("twosComplement"), .width(32)) divider_2 (
    .a(num2), .b(num1), .out(divider_2_out), .upper(div_upper));  // open: rem
  Negator #(.width(32)) negator_1 (.in(num1), .out(negator_1_out));
  // IntToFP #(.width(32)) inttofp_1: pin names not known; wires that end beside it: num1, inttofp_1_p2
  // FPToInt #(.width(32)) fptoint_1: pin names not known; wires that end beside it: num1, fptoint_1_p2
  Comparator #(.width(32)) comparator_1 (
    .a(num2), .b(num1), .gt(comparator_1_gt), .eq(comparator_1_eq), .lt(comparator_1_lt));
  Comparator #(.width(32)) comparator_2 (
    .a(num2), .b(num1), .gt(comparator_2_gt), .eq(comparator_2_eq), .lt(comparator_2_lt));
  // FPComparator fpcomparator_1: pin names not known; wires that end beside it: num2, num1, fpcomparator_1_p3, fpcomparator_1_p4, fpcomparator_1_p5
  // FPComparator fpcomparator_2: pin names not known; wires that end beside it: num2, num1, fpcomparator_2_p3, fpcomparator_2_p4, fpcomparator_2_p5
  FPAdder fpadder_1 (.a(num2), .b(num1), .out(fpadder_1_out));
  FPSubtractor fpsubtractor_1 (.a(num2), .b(num1), .out(fpsubtractor_1_out));
  FPMultiplier fpmultiplier_1 (.a(num1), .b(num1), .out(fpmultiplier_1_out));
  FPDivider fpdivider_1 (.a(num2), .b(num1), .out(fpdivider_1_out));
  // FPNegator fpnegator_1: pin names not known; wires that end beside it: num1, fpnegator_1_p2
  Multiplexer #(.select(4), .width(32)) multiplexer_1 (
    .in0(adder_1_out), .in1(subtractor_1_out), .in2(multiplier_1_out), .in3(multiplier_2_out),
    .in4(divider_1_out), .in5(divider_2_out), .in6(negator_1_out), .in7(fpadder_1_out),
    .in8(fpsubtractor_1_out), .in9(fpmultiplier_1_out), .in10(fpdivider_1_out), .in11(fpnegator_1_p2),
    .in12(inttofp_1_p2), .in13(fptoint_1_p2), .out(num_out), .sel(instruction));  // open: in14, in15
  Multiplexer #(.select(4)) multiplexer_2 (
    .in0(comparator_1_gt), .in1(comparator_1_eq), .in2(comparator_1_lt), .in3(comparator_2_gt),
    .in4(comparator_2_eq), .in5(comparator_2_lt), .in6(fpcomparator_1_p3), .in7(fpcomparator_1_p4),
    .in8(fpcomparator_1_p5), .in9(fpcomparator_2_p3), .in10(fpcomparator_2_p4), .in11(fpcomparator_2_p5),
    .out(comp_out), .sel(instruction));  // open: in12, in13, in14, in15
endmodule

module instruction_decoder (
  input  [3:0] sub_stage,
  input  [15:0] instruction,
  input  carry,
  input  comp,
  output PC_out,
  output jump,
  output PC_up,
  output RAM_adr_in,
  output RAM_in,
  output RAM_out,
  output num1_out,
  output num1_in,
  output num2_out,
  output num2_in,
  output [3:0] ALU_inst,
  output ALU_out,
  output IR_in,
  output IR_out
);
endmodule
