// Logisim project curcuit.circ as structural Verilog
module main (
);

  wire and_2_out, and_3_out, and_4_out, and_5_out, and_6_out, clck, clock_1_out, comparator_1_gt,
       comparator_2_gt, comparator_3_gt, comparator_4_gt, comparator_5_gt, dipswitch_1_sw1, HLT, not_1_out,
       not_2_out, not_3_out, not_4_out, not_5_out, not_6_out, reset, rgb_video_1_p3, rgb_video_2_p3,
       rgb_video_3_p3, rgb_video_4_p3, rgb_video_5_p3, rgb_video_6_p3, rgb_video_7_p3, rgb_video_8_p3,
       rgb_video_9_p3, rgb_video_10_p3, rgb_video_11_p3, rgb_video_12_p3;
  wire [3:0] bit_extender_5_out;
  wire [7:0] bit_extender_3_out, bit_extender_4_out;
  wire [11:0] bit_extender_1_out, bit_extender_2_out;
  wire [19:0] vgacard_1_h;
  wire [23:0] undriven, VRAM_dout;

  and and_1 (clck, clock_1_out, not_1_out);
  not not_1 (not_1_out, dipswitch_1_sw1);
  Clock clock_1 (.out(clock_1_out));
  DipSwitch #(.number(2)) dipswitch_1 (.sw1(dipswitch_1_sw1), .sw2(HLT));
  Button R (.out(reset));
  vgaCard vgacard_1 (.R(reset), .En(1'b1), .clock(clck), .nig(1'b0), .H(vgacard_1_h[9:0]), .V(vgacard_1_h[19:10]));
  RAM #(.addrWidth(20), .dataWidth(24), .enables("line"), .misaligned("true")) VRAM (
    .addr(vgacard_1_h), .clk(clck), .din(undriven), .dout(VRAM_dout));  // open: we
  Comparator #(.mode("unsigned"), .width(10)) comparator_1 (
    .a(vgacard_1_h[9:0]), .b(10'h100), .gt(comparator_1_gt));  // open: eq, lt
  Comparator #(.mode("unsigned"), .width(10)) comparator_2 (
    .a(vgacard_1_h[9:0]), .b(10'h200), .gt(comparator_2_gt));  // open: eq, lt
  Comparator #(.mode("unsigned"), .width(10)) comparator_3 (
    .a(vgacard_1_h[9:0]), .b(10'h300), .gt(comparator_3_gt));  // open: eq, lt
  Comparator #(.mode("unsigned"), .width(10)) comparator_4 (
    .a(vgacard_1_h[19:10]), .b(10'h100), .gt(comparator_4_gt));  // open: eq, lt
  Comparator #(.mode("unsigned"), .width(10)) comparator_5 (
    .a(vgacard_1_h[19:10]), .b(10'h200), .gt(comparator_5_gt));  // open: eq, lt
  assign bit_extender_1_out = {{2{vgacard_1_h[19]}}, vgacard_1_h[19:10]};  // Bit_Extender bit_extender_1
  assign bit_extender_2_out = {{2{vgacard_1_h[9]}}, vgacard_1_h[9:0]};  // Bit_Extender bit_extender_2
  not not_2 (not_2_out, comparator_1_gt);
  not not_3 (not_3_out, comparator_2_gt);
  not not_4 (not_4_out, comparator_3_gt);
  not not_5 (not_5_out, comparator_4_gt);
  not not_6 (not_6_out, comparator_5_gt);
  // Probe on vgacard_1_h[19:10]
  // Probe on vgacard_1_h[9:0]
  and and_2 (and_2_out, not_2_out, not_3_out, not_4_out);
  and and_3 (and_3_out, comparator_1_gt, not_3_out, not_4_out);
  and and_4 (and_4_out, comparator_2_gt, not_4_out);
  and and_5 (and_5_out, not_5_out, not_6_out);
  and and_6 (and_6_out, comparator_4_gt, not_6_out);
  Bit_Extender #(.in_width(10), .out_width(8)) bit_extender_3 (.in(vgacard_1_h[19:10]), .out(bit_extender_3_out));
  Bit_Extender #(.in_width(10), .out_width(8)) bit_extender_4 (.in(vgacard_1_h[9:0]), .out(bit_extender_4_out));
  Bit_Extender #(.out_width(4), .\type ("zero")) bit_extender_5 (.in(bit_extender_3_out), .out(bit_extender_5_out));
  // RGB_Video #(.height(256), .reset("Synchronous"), .scale(1), .width(256)) rgb_video_1: pin names not known; wires that end beside it: reset, clck, rgb_video_1_p3, bit_extender_4_out, bit_extender_3_out, {bit_extender_2_out, bit_extender_1_out}
  and and_7 (rgb_video_1_p3, and_2_out, and_5_out);
  // RGB_Video #(.height(256), .reset("Synchronous"), .scale(1), .width(256)) rgb_video_2: pin names not known; wires that end beside it: reset, clck, rgb_video_2_p3, bit_extender_4_out, bit_extender_3_out, VRAM_dout
  and and_8 (rgb_video_2_p3, and_2_out, and_6_out);
  // RGB_Video #(.height(16), .reset("Synchronous"), .scale(1), .width(256)) rgb_video_3: pin names not known; wires that end beside it: reset, clck, rgb_video_3_p3, bit_extender_4_out, bit_extender_5_out, VRAM_dout
  and and_9 (rgb_video_3_p3, and_2_out, comparator_5_gt);
  // RGB_Video #(.height(256), .reset("Synchronous"), .scale(1), .width(256)) rgb_video_4: pin names not known; wires that end beside it: reset, clck, rgb_video_4_p3, bit_extender_4_out, bit_extender_3_out, {bit_extender_2_out, bit_extender_1_out}
  and and_10 (rgb_video_4_p3, and_3_out, and_5_out);
  // RGB_Video #(.height(256), .reset("Synchronous"), .scale(1), .width(256)) rgb_video_5: pin names not known; wires that end beside it: reset, clck, rgb_video_5_p3, bit_extender_4_out, bit_extender_3_out, VRAM_dout
  and and_11 (rgb_video_5_p3, and_3_out, and_6_out);
  // RGB_Video #(.height(16), .reset("Synchronous"), .scale(1), .width(256)) rgb_video_6: pin names not known; wires that end beside it: reset, clck, rgb_video_6_p3, bit_extender_4_out, bit_extender_5_out, VRAM_dout
  and and_12 (rgb_video_6_p3, and_3_out, comparator_5_gt);
  // RGB_Video #(.height(256), .reset("Synchronous"), .scale(1), .width(256)) rgb_video_7: pin names not known; wires that end beside it: reset, clck, rgb_video_7_p3, bit_extender_4_out, bit_extender_3_out, {bit_extender_2_out, bit_extender_1_out}
  and and_13 (rgb_video_7_p3, and_4_out, and_5_out);
  // RGB_Video #(.height(256), .reset("Synchronous"), .scale(1), .width(256)) rgb_video_8: pin names not known; wires that end beside it: reset, clck, rgb_video_8_p3, bit_extender_4_out, bit_extender_3_out, VRAM_dout
  and and_14 (rgb_video_8_p3, and_4_out, and_6_out);
  // RGB_Video #(.height(16), .reset("Synchronous"), .scale(1), .width(256)) rgb_video_9: pin names not known; wires that end beside it: reset, clck, rgb_video_9_p3, bit_extender_4_out, bit_extender_5_out, VRAM_dout
  and and_15 (rgb_video_9_p3, and_4_out, comparator_5_gt);
  // RGB_Video #(.height(256), .reset("Synchronous"), .scale(1), .width(256)) rgb_video_10: pin names not known; wires that end beside it: reset, clck, rgb_video_10_p3, bit_extender_4_out, bit_extender_3_out, {bit_extender_2_out, bit_extender_1_out}
  // RGB_Video #(.height(256), .reset("Synchronous"), .scale(1), .width(256)) rgb_video_11: pin names not known; wires that end beside it: reset, clck, rgb_video_11_p3, bit_extender_4_out, bit_extender_3_out, VRAM_dout
  // RGB_Video #(.height(16), .reset("Synchronous"), .scale(1), .width(256)) rgb_video_12: pin names not known; wires that end beside it: reset, clck, rgb_video_12_p3, bit_extender_4_out, bit_extender_5_out, VRAM_dout
  and and_16 (rgb_video_10_p3, comparator_3_gt, and_5_out);
  and and_17 (rgb_video_11_p3, comparator_3_gt, and_6_out);
  and and_18 (rgb_video_12_p3, comparator_3_gt, comparator_5_gt);
endmodule

module ProgramCounter (
  input  [31:0] JmpAddr,
  input  Reset,
  input  Jmp,
  input  Clock,
  output [31:0] ip
);

  wire [31:0] adder_1_out, multiplexer_1_out;

  Adder #(.width(32)) adder_1 (.a(ip), .b(32'h1), .out(adder_1_out));  // open: cin, cout
  Multiplexer #(.width(32)) multiplexer_1 (.in0(adder_1_out), .in1(JmpAddr), .out(multiplexer_1_out), .sel(Jmp));
  Register #(.width(32)) PC (.D(multiplexer_1_out), .en(1'b1), .Q(ip), .clk(Clock), .clr(Reset));
endmodule

module CPU (
  input  reset,
  input  Input_1,
  input  HLT,
  output [2:0] ODD,
  output [31:0] OD1,
  output [31:0] OD2
);

  wire ALU_Calc, and_1_out, and_2_out, and_3_out, ARI, ARO, buffer_1_out, Button_1_out, clck, DRW, HLT_t,
       InstrDecoder_1_jf, IRAO, IRI, IRO, JMP, MI, ML, MO, nor_1_out, OD1W, OD2W, ODW, OEn, PCO, PCUp,
       reset_t, SR1O, SR2O;
  wire [2:0] ALU_1_co, flags, ODD_t;
  wire [3:0] ALU_OP, DRID, InstrDecoder_1_op, SR1ID, SR2ID;
  wire [23:0] adr_bus, bit_extender_2_out, PC_q, register_1_q;
  wire [31:0] ALU_1_a_o, bit_extender_1_out, data_bus, IR_q, RAM_1_dout, SR1, SR2;

  Button Button_1 (.out(Button_1_out));
  or or_1 (reset_t, Button_1_out, reset);
  Clock clock_1 (.out(clck));
  Register #(.width(24)) register_1 (.D(adr_bus), .en(ARI), .clk(clck), .Q(register_1_q), .clr(reset_t));
  RAM #(.addrWidth(24), .dataWidth(32)) RAM_1 (
    .addr(adr_bus), .we(MI), .oe(buffer_1_out), .clk(clck), .din(data_bus), .dout(RAM_1_dout));
  buf buffer_1 (buffer_1_out, ML);
  Register #(.width(32)) IR (.D(data_bus), .en(IRI), .clk(clck), .Q(IR_q), .clr(reset_t));
  Counter #(.max('hffffff), .ongoal("continue"), .width(24)) PC (
    .load(JMP), .D(adr_bus), .count(PCUp), .Q(PC_q), .up(1'b1), .clk(clck), .clr(reset_t));  // open: carry
  assign adr_bus = ARO ? register_1_q : 24'bz;  // Controlled_Buffer controlled_buffer_1
  assign adr_bus = PCO ? PC_q : 24'bz;  // Controlled_Buffer controlled_buffer_2
  assign bit_extender_1_out = {{8{1'b0}}, IR_q[23:0]};  // Bit_Extender bit_extender_1
  assign data_bus = IRO ? bit_extender_1_out : 32'bz;  // Controlled_Buffer controlled_buffer_3
  assign adr_bus = IRAO ? IR_q[23:0] : 24'bz;  // Controlled_Buffer controlled_buffer_4
  assign data_bus = MO ? RAM_1_dout : 32'bz;  // Controlled_Buffer controlled_buffer_5
  ALU ALU_1 (
    .Carry(1'b0), .Op(ALU_OP), .N1(SR1), .N2(SR2), .CO(ALU_1_co[0]), .zero(ALU_1_co[1]), .A_O(ALU_1_a_o),
    .Comp(ALU_1_co[2]));
  assign data_bus = ALU_Calc ? ALU_1_a_o : 32'bz;  // Controlled_Buffer controlled_buffer_6
  RegisterBank RegisterBank_1 (
    .C(clck), .R(reset_t), .W(DRW), .RS1(SR1ID), .RS2(SR2ID), .DR(DRID), .DRD(data_bus), .S1(SR1), .S2(SR2));
  Register #(.width(3)) u_Flags (.D(ALU_1_co), .en(ALU_Calc), .clk(clck), .Q(flags), .clr(reset_t));
  assign data_bus = SR1O ? SR1 : 32'bz;  // Controlled_Buffer controlled_buffer_7
  Bit_Extender #(.in_width(32), .out_width(24)) bit_extender_2 (.in(SR2), .out(bit_extender_2_out));
  assign adr_bus = SR2O ? bit_extender_2_out : 24'bz;  // Controlled_Buffer controlled_buffer_8
  InstrDecoder InstrDecoder_1 (
    .IR(IR_q), .flags(flags), .ALUOP(ALU_OP), .DR(DRID), .SR2(SR2ID), .SR1(SR1ID), .DDI(ODW), .OD1I(OD1W),
    .OD2I(OD2W), .ODD(ODD_t), .OP(InstrDecoder_1_op), .JF(InstrDecoder_1_jf));
  Hex_Digit_Display #(.decimalPoint("false")) Hex_Digit_Display_1 (.value(InstrDecoder_1_op));
  nor nor_1 (nor_1_out, HLT, HLT_t);
  and and_1 (and_1_out, ODW, OEn);
  and and_2 (and_2_out, OD1W, OEn);
  and and_3 (and_3_out, OD2W, OEn);
  Executor Executor_1 (
    .OP(InstrDecoder_1_op), .JF(InstrDecoder_1_jf), .clock(clck), .reset(reset_t), .Istop(nor_1_out),
    .JMP(JMP), .PCU(PCUp), .PCO(PCO), .DRW(DRW), .SR1O(SR1O), .SR2O(SR2O), .ALUCalc(ALU_Calc), .MI(MI),
    .ML(ML), .MO(MO), .IRI(IRI), .IRO(IRO), .IRAO(IRAO), .ARI(ARI), .ARO(ARO), .OEn(OEn), .HLT(HLT_t));
  Register #(.width(3)) register_2 (.D(ODD_t), .en(and_1_out), .clk(clck), .Q(ODD), .clr(reset_t));
  Register #(.width(32)) register_3 (.D(data_bus), .en(and_2_out), .clk(clck), .Q(OD1), .clr(reset_t));
  Register #(.width(32)) register_4 (.D(data_bus), .en(and_3_out), .clk(clck), .Q(OD2), .clr(reset_t));
endmodule

module ALU (
  input  Carry,
  input  [3:0] Op,
  input  [31:0] N1,
  input  [31:0] N2,
  output CO,
  output zero,
  output [31:0] A_O,
  output Comp
);

  wire comparator_1_eq, comparator_1_gt, comparator_1_lt, or_2_out, or_3_out;
  wire [4:0] bit_extender_1_out, bit_extender_2_out, bit_extender_3_out, bit_extender_4_out,
       bit_extender_5_out;
  wire [31:0] adder_1_out, and_1_out, multiplier_1_out, nand_1_out, negator_1_out, not_1_out, or_1_out,
       shifter_1_out, shifter_2_out, shifter_3_out, shifter_4_out, shifter_5_out, subtractor_1_out,
       xnor_1_out, xor_1_out;

  Bit_Extender #(.in_width(32), .out_width(5), .\type ("zero")) bit_extender_1 (.in(N2), .out(bit_extender_1_out));
  Bit_Extender #(.in_width(32), .out_width(5), .\type ("zero")) bit_extender_2 (.in(N2), .out(bit_extender_2_out));
  Bit_Extender #(.in_width(32), .out_width(5), .\type ("zero")) bit_extender_3 (.in(N2), .out(bit_extender_3_out));
  Bit_Extender #(.in_width(32), .out_width(5), .\type ("zero")) bit_extender_4 (.in(N2), .out(bit_extender_4_out));
  Bit_Extender #(.in_width(32), .out_width(5), .\type ("zero")) bit_extender_5 (.in(N2), .out(bit_extender_5_out));
  Adder #(.width(32)) adder_1 (.a(N1), .b(N2), .out(adder_1_out), .cin(Carry), .cout(CO));
  Subtractor #(.width(32)) subtractor_1 (.a(N1), .b(N2), .out(subtractor_1_out), .bin(1'b0));  // open: bout
  Multiplier #(.width(32)) multiplier_1 (.a(N1), .b(N2), .out(multiplier_1_out), .cin({32{1'b0}}));  // open: cout
  Negator #(.width(32)) negator_1 (.in(N1), .out(negator_1_out));
  assign and_1_out = N1 & N2;  // AND_Gate and_1, 32 bits wide
  assign or_1_out = N1 | N2;  // OR_Gate or_1, 32 bits wide
  assign not_1_out = ~N1;  // NOT_Gate not_1, 32 bits wide
  assign nand_1_out = ~(N1 & N2);  // NAND_Gate nand_1, 32 bits wide
  assign xor_1_out = N1 ^ N2;  // XOR_Gate xor_1, 32 bits wide
  assign xnor_1_out = ~(N1 ^ N2);  // XNOR_Gate xnor_1, 32 bits wide
  Shifter #(.width(32)) shifter_1 (.in(N1), .\dist (bit_extender_1_out), .out(shifter_1_out));
  Shifter #(.shift("lr"), .width(32)) shifter_2 (.in(N1), .\dist (bit_extender_2_out), .out(shifter_2_out));
  Shifter #(.shift("ar"), .width(32)) shifter_3 (.in(N1), .\dist (bit_extender_3_out), .out(shifter_3_out));
  Shifter #(.shift("rl"), .width(32)) shifter_4 (.in(N1), .\dist (bit_extender_4_out), .out(shifter_4_out));
  Shifter #(.shift("rr"), .width(32)) shifter_5 (.in(N1), .\dist (bit_extender_5_out), .out(shifter_5_out));
  Comparator #(.mode("unsigned"), .width(32)) comparator_1 (
    .a(N1), .b(N2), .gt(comparator_1_gt), .eq(comparator_1_eq), .lt(comparator_1_lt));
  or or_2 (or_2_out, comparator_1_gt, comparator_1_eq);
  or or_3 (or_3_out, comparator_1_eq, comparator_1_lt);
  Multiplexer #(.select(4), .width(32)) multiplexer_1 (
    .in0(adder_1_out), .in1(subtractor_1_out), .in2(multiplier_1_out), .in3(negator_1_out), .in4(and_1_out),
    .in5(or_1_out), .in6(not_1_out), .in7(nand_1_out), .in8(xor_1_out), .in9(xnor_1_out),
    .in10(shifter_1_out), .in11(shifter_2_out), .in12(shifter_3_out), .in13(shifter_4_out),
    .in14(shifter_5_out), .in15({32{1'b0}}), .out(A_O), .sel(Op));
  Multiplexer #(.select(4)) multiplexer_2 (
    .in0(comparator_1_gt), .in1(comparator_1_eq), .in2(comparator_1_lt), .in3(or_2_out), .in4(or_3_out),
    .in5(1'b0), .in6(1'b0), .in7(1'b0), .in8(1'b0), .in9(1'b0), .in10(1'b0), .in11(1'b0), .in12(1'b0),
    .in13(1'b0), .in14(1'b0), .in15(1'b0), .out(Comp), .sel(Op));
  and and_2 (zero, ~1'b0, ~A_O[0], ~A_O[1], ~A_O[2], ~A_O[3], ~A_O[4], ~A_O[5], ~A_O[6], ~A_O[7], ~A_O[8], ~A_O[9], ~A_O[10], ~A_O[11], ~A_O[12], ~A_O[13], ~A_O[14], ~A_O[15], ~A_O[16], ~A_O[17], ~A_O[18], ~A_O[19], ~A_O[20], ~A_O[21], ~A_O[22], ~A_O[23], ~A_O[24], ~A_O[25], ~A_O[26], ~A_O[27], ~A_O[28], ~A_O[29], ~A_O[30], ~A_O[31]);  // AND_Gate
endmodule

module RegisterBank (
  input  C,
  input  R,
  input  W,
  input  [3:0] RS1,
  input  [3:0] RS2,
  input  [3:0] DR,
  input  [31:0] DRD,
  output [31:0] S1,
  output [31:0] S2
);

  wire and_1_out, and_2_out, and_3_out, and_4_out, and_5_out, and_6_out, and_7_out, and_8_out, and_9_out,
       and_10_out, and_11_out, and_12_out, and_13_out, and_14_out, and_15_out, and_16_out, decoder_1_out0,
       decoder_1_out1, decoder_1_out2, decoder_1_out3, decoder_1_out4, decoder_1_out5, decoder_1_out6,
       decoder_1_out7, decoder_1_out8, decoder_1_out9, decoder_1_out10, decoder_1_out11, decoder_1_out12,
       decoder_1_out13, decoder_1_out14, decoder_1_out15;
  wire [31:0] R0_q, R1_q, R2_q, R3_q, R4_q, R5_q, R6_q, R7_q, R8_q, R9_q, R10_q, R11_q, R12_q, R13_q, R14_q,
       Tmp_q;

  Decoder #(.enable("false"), .select(4)) decoder_1 (
    .out0(decoder_1_out0), .out1(decoder_1_out1), .out2(decoder_1_out2), .out3(decoder_1_out3),
    .out4(decoder_1_out4), .out5(decoder_1_out5), .out6(decoder_1_out6), .out7(decoder_1_out7),
    .out8(decoder_1_out8), .out9(decoder_1_out9), .out10(decoder_1_out10), .out11(decoder_1_out11),
    .out12(decoder_1_out12), .out13(decoder_1_out13), .out14(decoder_1_out14), .out15(decoder_1_out15),
    .sel(DR));
  Register #(.width(32)) R0 (.D(DRD), .en(and_1_out), .clk(C), .Q(R0_q), .clr(R));
  and and_1 (and_1_out, decoder_1_out0, W);
  Register #(.width(32)) R1 (.D(DRD), .en(and_2_out), .clk(C), .Q(R1_q), .clr(R));
  and and_2 (and_2_out, decoder_1_out1, W);
  Register #(.width(32)) R2 (.D(DRD), .en(and_3_out), .clk(C), .Q(R2_q), .clr(R));
  and and_3 (and_3_out, decoder_1_out2, W);
  and and_4 (and_4_out, decoder_1_out3, W);
  and and_5 (and_5_out, decoder_1_out4, W);
  and and_6 (and_6_out, decoder_1_out5, W);
  Register #(.width(32)) R3 (.D(DRD), .en(and_4_out), .clk(C), .Q(R3_q), .clr(R));
  Register #(.width(32)) R4 (.D(DRD), .en(and_5_out), .clk(C), .Q(R4_q), .clr(R));
  Register #(.width(32)) R5 (.D(DRD), .en(and_6_out), .clk(C), .Q(R5_q), .clr(R));
  Register #(.width(32)) R6 (.D(DRD), .en(and_7_out), .clk(C), .Q(R6_q), .clr(R));
  and and_7 (and_7_out, decoder_1_out6, W);
  Register #(.width(32)) R7 (.D(DRD), .en(and_8_out), .clk(C), .Q(R7_q), .clr(R));
  and and_8 (and_8_out, decoder_1_out7, W);
  Register #(.width(32)) R8 (.D(DRD), .en(and_9_out), .clk(C), .Q(R8_q), .clr(R));
  and and_9 (and_9_out, decoder_1_out8, W);
  Register #(.width(32)) R9 (.D(DRD), .en(and_10_out), .clk(C), .Q(R9_q), .clr(R));
  and and_10 (and_10_out, decoder_1_out9, W);
  Register #(.width(32)) R10 (.D(DRD), .en(and_11_out), .clk(C), .Q(R10_q), .clr(R));
  and and_11 (and_11_out, decoder_1_out10, W);
  and and_12 (and_12_out, decoder_1_out11, W);
  and and_13 (and_13_out, decoder_1_out12, W);
  and and_14 (and_14_out, decoder_1_out13, W);
  Register #(.width(32)) R11 (.D(DRD), .en(and_12_out), .clk(C), .Q(R11_q), .clr(R));
  Register #(.width(32)) R12 (.D(DRD), .en(and_13_out), .clk(C), .Q(R12_q), .clr(R));
  Register #(.width(32)) R13 (.D(DRD), .en(and_14_out), .clk(C), .Q(R13_q), .clr(R));
  Register #(.width(32)) R14 (.D(DRD), .en(and_15_out), .clk(C), .Q(R14_q), .clr(R));
  and and_15 (and_15_out, decoder_1_out14, W);
  Register #(.width(32)) Tmp (.D(DRD), .en(and_16_out), .clk(C), .Q(Tmp_q), .clr(R));
  and and_16 (and_16_out, decoder_1_out15, W);
  Multiplexer #(.select(4), .width(32)) multiplexer_1 (
    .in0(R0_q), .in1(R1_q), .in2(R2_q), .in3(R3_q), .in4(R4_q), .in5(R5_q), .in6(R6_q), .in7(R7_q),
    .in8(R8_q), .in9(R9_q), .in10(R10_q), .in11(R11_q), .in12(R12_q), .in13(R13_q), .in14(R14_q),
    .in15(Tmp_q), .out(S1), .sel(RS1));
  Multiplexer #(.select(4), .width(32)) multiplexer_2 (
    .in0(R0_q), .in1(R1_q), .in2(R2_q), .in3(R3_q), .in4(R4_q), .in5(R5_q), .in6(R6_q), .in7(R7_q),
    .in8(R8_q), .in9(R9_q), .in10(R10_q), .in11(R11_q), .in12(R12_q), .in13(R13_q), .in14(R14_q),
    .in15(Tmp_q), .out(S2), .sel(RS2));

  // Notes on the sheet:
  //   R0
  //   R1
  //   R2
  //   R3
  //   R4
  //   R5
  //   R6
  //   R7
  //   R8\
  //   R9
  //   R10
  //   R11
  //   R12
  //   R13
  //   R14
  //   Tmp/Dump
endmodule

module InstrDecoder (
  input  [31:0] IR,
  input  [2:0] flags,
  output [3:0] ALUOP,
  output [3:0] DR,
  output [3:0] SR2,
  output [3:0] SR1,
  output DDI,
  output OD1I,
  output OD2I,
  output [2:0] ODD,
  output [3:0] OP,
  output JF
);

  wire and_2_out, and_3_out, InstrDecoderCA_1_sr1tdr, not_1_out, not_2_out;

  not not_1 (not_1_out, IR[7]);
  not not_2 (not_2_out, IR[8]);
  and and_1 (DDI, IR[7], not_2_out);
  and and_2 (and_2_out, not_1_out, not_2_out);
  and and_3 (and_3_out, IR[7], IR[8]);
  or or_1 (OD1I, and_2_out, and_3_out);
  InstrDecoderCA InstrDecoderCA_1 (
    .OP(IR[31:28]), .JMPIF(IR[26:24]), .carry(flags[0]), .Zero(flags[1]), .comp(flags[2]), .POP(OP),
    .SR1TDR(InstrDecoderCA_1_sr1tdr));
  Multiplexer #(.width(4)) multiplexer_1 (.in0(IR[19:16]), .in1(IR[27:24]), .out(DR), .sel(InstrDecoderCA_1_sr1tdr));

  assign ALUOP = IR[15:12];
  assign JF = IR[27];
  assign OD2I = IR[8];
  assign ODD = IR[11:9];
  assign SR1 = IR[27:24];
  assign SR2 = IR[23:20];

  // Other names for the same wires on the sheet: carry = flags[0]; Zero = flags[1]; comp = flags[2]
endmodule

module counter_3_bit (
  input  C,
  input  R,
  output [2:0] count
);

  wire j_k_ff_1_qn, j_k_ff_2_qn, j_k_ff_3_qn, not_1_out, not_2_out, not_3_out;

  J_K_Flip_Flop j_k_ff_1 (
    .J(j_k_ff_1_qn), .K(not_1_out), .clk(C), .Q(count[0]), .Qn(j_k_ff_1_qn), .reset(R));  // open: preset
  not not_1 (not_1_out, j_k_ff_1_qn);
  J_K_Flip_Flop j_k_ff_2 (
    .J(j_k_ff_2_qn), .K(not_2_out), .clk(j_k_ff_1_qn), .Q(count[1]), .Qn(j_k_ff_2_qn), .reset(R));  // open: preset
  not not_2 (not_2_out, j_k_ff_2_qn);
  J_K_Flip_Flop j_k_ff_3 (
    .J(j_k_ff_3_qn), .K(not_3_out), .clk(j_k_ff_2_qn), .Q(count[2]), .Qn(j_k_ff_3_qn), .reset(R));  // open: preset
  not not_3 (not_3_out, j_k_ff_3_qn);
endmodule

module InstrDecoderCA (
  input  [3:0] OP,
  input  [2:0] JMPIF,
  input  carry,
  input  Zero,
  input  comp,
  output [3:0] POP,
  output SR1TDR
);

  wire and_1_out, and_2_out, and_3_out, and_4_out, and_5_out, and_6_out, and_7_out, and_8_out, and_9_out,
       and_10_out, and_11_out, and_12_out, and_13_out, and_14_out, and_15_out, and_16_out, and_17_out,
       and_18_out, not_1_out, not_2_out, not_3_out, not_4_out, not_5_out, not_6_out, not_7_out, not_8_out,
       not_9_out;

  not not_1 (not_1_out, OP[3]);
  not not_2 (not_2_out, OP[1]);
  not not_3 (not_3_out, OP[0]);
  not not_4 (not_4_out, JMPIF[2]);
  not not_5 (not_5_out, JMPIF[1]);
  not not_6 (not_6_out, JMPIF[0]);
  not not_7 (not_7_out, carry);
  not not_8 (not_8_out, Zero);
  not not_9 (not_9_out, comp);
  and and_1 (and_1_out, OP[1], not_3_out);
  and and_2 (and_2_out, OP[1], not_4_out, not_5_out, carry);
  and and_3 (and_3_out, OP[1], not_4_out, not_6_out, not_7_out);
  and and_4 (and_4_out, OP[1], JMPIF[2], not_5_out, JMPIF[0], Zero);
  and and_5 (and_5_out, OP[1], JMPIF[2], JMPIF[1], not_6_out, not_8_out);
  and and_6 (and_6_out, OP[2], OP[1]);
  and and_7 (and_7_out, OP[3], OP[1]);
  and and_8 (and_8_out, OP[1], not_4_out, JMPIF[1], JMPIF[0], comp);
  and and_9 (and_9_out, OP[1], not_5_out, not_6_out, not_9_out);
  and and_10 (and_10_out, not_2_out, OP[0]);
  and and_11 (and_11_out, OP[0], not_4_out, not_5_out, carry);
  and and_12 (and_12_out, OP[0], not_4_out, not_6_out, not_7_out);
  and and_13 (and_13_out, OP[0], JMPIF[2], not_5_out, JMPIF[0], Zero);
  and and_14 (and_14_out, OP[0], JMPIF[2], JMPIF[1], not_6_out, not_8_out);
  and and_15 (and_15_out, OP[2], OP[0]);
  and and_16 (and_16_out, OP[3], OP[0]);
  and and_17 (and_17_out, OP[0], not_4_out, JMPIF[1], JMPIF[0], comp);
  and and_18 (and_18_out, OP[0], not_5_out, not_6_out, not_9_out);
  and and_19 (SR1TDR, not_1_out, OP[2], not_3_out);
  or or_1 (POP[1], and_1_out, and_2_out, and_3_out, and_4_out, and_5_out, and_6_out, and_7_out, and_8_out, and_9_out);
  or or_2 (POP[0], and_10_out, and_11_out, and_12_out, and_13_out, and_14_out, and_15_out, and_16_out, and_17_out, and_18_out);

  assign POP[3:2] = OP[3:2];
endmodule

module Executor (
  input  [3:0] OP,
  input  JF,
  input  clock,
  input  reset,
  input  Istop,
  output JMP,
  output PCU,
  output PCO,
  output DRW,
  output SR1O,
  output SR2O,
  output ALUCalc,
  output MI,
  output ML,
  output MO,
  output IRI,
  output IRO,
  output IRAO,
  output ARI,
  output ARO,
  output OEn,
  output HLT
);

  wire ExecutorCA_1_jsc1, ExecutorCA_1_rsc, or_1_out;
  wire [2:0] counter_1_q;

  or or_1 (or_1_out, reset, ExecutorCA_1_rsc);
  Counter #(.max('h7), .width(3)) counter_1 (
    .clr(or_1_out), .load(ExecutorCA_1_jsc1), .up(1'b1), .count(Istop), .clk(clock), .D(3'b001),
    .Q(counter_1_q));  // open: carry
  ExecutorCA ExecutorCA_1 (
    .OP(OP), .JF(JF), .SBC(counter_1_q), .JMP(JMP), .PCU(PCU), .PCO(PCO), .DRW(DRW), .SR1O(SR1O),
    .SR2O(SR2O), .ALUCalc(ALUCalc), .MI(MI), .ML(ML), .MO(MO), .IRI(IRI), .IRO(IRO), .IRAO(IRAO), .ARI(ARI),
    .ARO(ARO), .OEn(OEn), .HLT(HLT), .JSC1(ExecutorCA_1_jsc1), .RSC(ExecutorCA_1_rsc));
endmodule

module ExecutorCA (
  input  [3:0] OP,
  input  JF,
  input  [2:0] SBC,
  output JMP,
  output PCU,
  output PCO,
  output DRW,
  output SR1O,
  output SR2O,
  output ALUCalc,
  output MI,
  output ML,
  output MO,
  output IRI,
  output IRO,
  output IRAO,
  output ARI,
  output ARO,
  output OEn,
  output HLT,
  output JSC1,
  output RSC
);

  wire and_1_out, and_2_out, and_3_out, and_4_out, and_5_out, and_6_out, and_7_out, and_8_out, and_9_out,
       and_10_out, and_11_out, and_12_out, and_13_out, and_14_out, and_15_out, and_16_out, and_17_out,
       and_18_out, and_19_out, and_20_out, and_21_out, and_22_out, and_23_out, and_24_out, and_25_out,
       and_26_out, and_27_out, and_28_out, and_29_out, and_30_out, and_31_out, and_32_out, and_33_out,
       and_34_out, and_35_out, and_38_out, and_39_out, and_40_out, and_41_out, and_42_out, and_43_out,
       and_44_out, and_45_out, and_47_out, and_48_out, and_49_out, and_50_out, and_51_out, and_52_out,
       and_53_out, and_54_out, and_55_out, and_56_out, and_57_out, and_58_out, and_59_out, and_60_out,
       and_61_out, not_1_out, not_2_out, not_3_out, not_4_out, not_5_out, not_6_out, not_7_out, not_8_out;

  not not_1 (not_1_out, OP[3]);
  not not_2 (not_2_out, OP[2]);
  not not_3 (not_3_out, OP[1]);
  not not_4 (not_4_out, OP[0]);
  not not_5 (not_5_out, JF);
  not not_6 (not_6_out, SBC[2]);
  not not_7 (not_7_out, SBC[1]);
  not not_8 (not_8_out, SBC[0]);
  and and_1 (and_1_out, not_1_out, not_2_out, OP[1], OP[0], not_5_out, not_6_out, SBC[1], SBC[0]);
  and and_2 (and_2_out, not_1_out, not_2_out, OP[1], OP[0], JF, not_6_out, SBC[1], not_8_out);
  and and_3 (and_3_out, not_6_out, not_7_out, SBC[0]);
  and and_4 (and_4_out, not_1_out, not_2_out, OP[1], OP[0], not_5_out, not_6_out, SBC[0]);
  and and_5 (and_5_out, not_1_out, not_2_out, OP[1], OP[0], JF, not_6_out, SBC[1], not_8_out);
  and and_6 (and_6_out, not_6_out, not_7_out, not_8_out);
  and and_7 (and_7_out, not_1_out, OP[2], not_3_out, not_4_out, not_6_out, SBC[1], SBC[0]);
  and and_8 (and_8_out, not_2_out, not_3_out, OP[0], not_6_out, not_8_out);
  and and_9 (and_9_out, not_1_out, OP[2], not_3_out, OP[0], not_7_out, not_8_out);
  and and_10 (and_10_out, not_1_out, OP[1], not_4_out, not_6_out, not_8_out);
  and and_11 (and_11_out, not_2_out, OP[1], not_4_out, not_6_out, not_8_out);
  and and_12 (and_12_out, not_2_out, not_3_out, OP[0], not_6_out, SBC[1], not_8_out);
  and and_13 (and_13_out, not_1_out, OP[2], OP[1], not_4_out, not_6_out, SBC[1], not_8_out);
  and and_14 (and_14_out, not_1_out, OP[2], not_3_out, not_4_out, not_6_out, SBC[1], SBC[0]);
  and and_15 (and_15_out, not_1_out, OP[2], not_3_out, OP[0], SBC[2], not_7_out, not_8_out);
  and and_16 (and_16_out, not_1_out, OP[2], OP[1], OP[0], not_6_out, SBC[1], not_8_out);
  and and_17 (and_17_out, OP[3], not_2_out, not_3_out, OP[0], not_6_out, SBC[1], not_8_out);
  and and_18 (and_18_out, OP[3], not_2_out, OP[1], not_4_out, not_6_out, SBC[1], not_8_out);
  and and_19 (and_19_out, OP[3], not_2_out, not_3_out, not_4_out, not_6_out, SBC[1], SBC[0]);
  and and_20 (and_20_out, not_1_out, not_2_out, OP[1], OP[0], not_5_out, not_6_out, SBC[1], not_8_out);
  and and_21 (and_21_out, not_1_out, OP[2], not_3_out, OP[0], not_6_out, SBC[1], not_8_out);
  and and_22 (and_22_out, OP[3], not_2_out, not_3_out, not_4_out, not_6_out, SBC[1], not_8_out);
  and and_23 (and_23_out, not_1_out, not_2_out, not_3_out, OP[0], not_6_out, SBC[1], not_8_out);
  and and_24 (and_24_out, not_1_out, not_2_out, OP[1], not_4_out, not_6_out, SBC[1], not_8_out);
  and and_25 (and_25_out, not_1_out, OP[2], OP[1], OP[0], not_6_out, SBC[1], not_8_out);
  and and_26 (and_26_out, OP[3], not_2_out, not_3_out, not_4_out, not_6_out, SBC[1], SBC[0]);
  and and_27 (and_27_out, not_6_out, not_7_out, not_8_out);
  and and_28 (and_28_out, not_2_out, not_3_out, OP[0], not_6_out, not_8_out);
  and and_29 (and_29_out, not_2_out, OP[1], not_4_out, not_6_out, not_8_out);
  and and_30 (and_30_out, not_1_out, OP[2], not_3_out, not_6_out, SBC[1], SBC[0]);
  and and_31 (and_31_out, not_1_out, OP[2], not_3_out, OP[0], not_7_out, not_8_out);
  and and_32 (and_32_out, not_1_out, OP[2], not_4_out, not_6_out, not_8_out);
  and and_33 (and_33_out, not_6_out, not_7_out, SBC[0]);
  and and_34 (and_34_out, not_1_out, OP[2], not_3_out, not_4_out, not_6_out, SBC[0]);
  and and_35 (and_35_out, not_1_out, OP[2], not_3_out, OP[0], SBC[2], not_7_out, not_8_out);
  and and_36 (IRI, not_6_out, not_7_out, SBC[0]);
  and and_37 (IRO, not_1_out, OP[2], OP[1], not_4_out, not_6_out, SBC[1], not_8_out);
  and and_38 (and_38_out, not_1_out, OP[2], not_3_out, not_4_out, not_6_out, SBC[1], not_8_out);
  and and_39 (and_39_out, not_1_out, OP[2], OP[1], OP[0], not_6_out, SBC[1], not_8_out);
  and and_40 (and_40_out, not_1_out, OP[1], OP[0], JF, not_6_out, SBC[1], not_8_out);
  and and_41 (and_41_out, not_1_out, not_2_out, OP[1], OP[0], not_5_out, not_6_out, SBC[1], not_8_out);
  and and_42 (and_42_out, not_1_out, OP[2], not_3_out, OP[0], not_6_out, SBC[1], not_8_out);
  and and_43 (and_43_out, OP[3], not_2_out, not_3_out, not_4_out, not_6_out, SBC[1], not_8_out);
  and and_44 (and_44_out, not_1_out, not_2_out, OP[1], OP[0], not_5_out, not_6_out, SBC[1], SBC[0]);
  and and_45 (and_45_out, not_1_out, OP[2], not_3_out, OP[0], not_6_out, SBC[1], SBC[0]);
  and and_46 (OEn, OP[3], not_2_out, OP[1], not_4_out, not_6_out, SBC[1], not_8_out);
  and and_47 (and_47_out, OP[3], OP[1], OP[0], not_6_out, SBC[1], not_8_out);
  and and_48 (and_48_out, OP[3], OP[2], not_6_out, SBC[1], not_8_out);
  and and_49 (and_49_out, not_1_out, OP[1], not_4_out, not_6_out, SBC[1], not_8_out);
  and and_50 (and_50_out, not_1_out, OP[2], not_3_out, not_4_out, not_6_out, SBC[1], SBC[0]);
  and and_51 (and_51_out, OP[3], not_2_out, OP[1], not_4_out, not_6_out, SBC[1], SBC[0]);
  and and_52 (and_52_out, not_1_out, not_2_out, not_3_out, OP[0], not_6_out, SBC[1], not_8_out);
  and and_53 (and_53_out, OP[3], not_2_out, not_3_out, OP[0], not_6_out, SBC[1], SBC[0]);
  and and_54 (and_54_out, not_1_out, OP[2], not_3_out, OP[0], SBC[2], not_7_out, not_8_out);
  and and_55 (and_55_out, not_1_out, not_2_out, not_3_out, not_4_out, not_6_out, SBC[1], SBC[0]);
  and and_56 (and_56_out, OP[3], OP[2], not_6_out, SBC[1], SBC[0]);
  and and_57 (and_57_out, OP[3], not_2_out, not_3_out, not_4_out, SBC[2], not_7_out, not_8_out);
  and and_58 (and_58_out, OP[2], OP[1], OP[0], not_6_out, SBC[1], SBC[0]);
  and and_59 (and_59_out, OP[3], OP[1], OP[0], not_6_out, SBC[1], SBC[0]);
  and and_60 (and_60_out, not_1_out, not_2_out, OP[1], OP[0], not_5_out, SBC[2], not_7_out, not_8_out);
  and and_61 (and_61_out, OP[1], OP[0], JF, not_6_out, SBC[1], SBC[0]);
  or or_1 (JMP, and_1_out, and_2_out);
  or or_2 (PCU, and_3_out, and_4_out, and_5_out);
  or or_3 (PCO, and_6_out, and_7_out, and_8_out, and_9_out, and_10_out, and_11_out);
  or or_4 (DRW, and_12_out, and_13_out, and_14_out, and_15_out);
  or or_5 (SR1O, and_16_out, and_17_out, and_18_out, and_19_out);
  or or_6 (SR2O, and_20_out, and_21_out, and_22_out);
  or or_7 (ALUCalc, and_23_out, and_24_out);
  or or_8 (MI, and_25_out, and_26_out);
  or or_9 (ML, and_27_out, and_28_out, and_29_out, and_30_out, and_31_out, and_32_out);
  or or_10 (MO, and_33_out, and_34_out, and_35_out);
  or or_11 (IRAO, and_38_out, and_39_out, and_40_out);
  or or_12 (ARI, and_41_out, and_42_out, and_43_out);
  or or_13 (ARO, and_44_out, and_45_out);
  or or_14 (HLT, and_47_out, and_48_out);
  or or_15 (JSC1, and_49_out, and_50_out, and_51_out, and_52_out, and_53_out, and_54_out);
  or or_16 (RSC, and_55_out, and_56_out, and_57_out, and_58_out, and_59_out, and_60_out, and_61_out);
endmodule

module MemAcces (
  input  [23:0] Adress,
  input  O,
  input  W,
  output ML,
  output MW,
  output ODcodW,
  output OD1W,
  output OD2W,
  output OD3W
);

  wire and_1_out, undriven;
  wire [2:0] undriven_2;

  and and_1 (and_1_out, Adress[23], Adress[22], Adress[21], Adress[20], Adress[19], Adress[18], Adress[17], Adress[16], Adress[15], Adress[14], Adress[13], Adress[12], Adress[11], Adress[10], Adress[9], Adress[8], Adress[7], Adress[6], Adress[5], Adress[4], Adress[3]);
  MemAccesCA MemAccesCA_1 (
    .regOrMem(undriven), .regID(undriven_2), .O(O), .W(W), .ML(ML), .MW(MW), .ODcodW(ODcodW), .OD1W(OD1W),
    .OD2W(OD2W), .OD3W(OD3W));
endmodule

module MemAccesCA (
  input  regOrMem,
  input  [2:0] regID,
  input  O,
  input  W,
  output ML,
  output MW,
  output ODcodW,
  output OD1W,
  output OD2W,
  output OD3W
);

  wire not_1_out, not_2_out, not_3_out, not_4_out;

  not not_1 (not_1_out, regOrMem);
  not not_2 (not_2_out, regID[2]);
  not not_3 (not_3_out, regID[1]);
  not not_4 (not_4_out, regID[0]);
  and and_1 (ML, not_1_out, O);
  and and_2 (MW, not_1_out, W);
  and and_3 (ODcodW, regOrMem, not_2_out, not_3_out, not_4_out, W);
  and and_4 (OD1W, regOrMem, not_2_out, not_3_out, regID[0], W);
  and and_5 (OD2W, regOrMem, not_2_out, regID[1], not_4_out, W);
  and and_6 (OD3W, regOrMem, not_2_out, regID[1], regID[0], W);
endmodule

module test (
  input  p256,
  input  p512,
  input  p768,
  output x1,
  output x2,
  output x3,
  output x4
);

  wire not_1_out, not_2_out, not_3_out;

  not not_1 (not_1_out, p256);
  not not_2 (not_2_out, p512);
  not not_3 (not_3_out, p768);
  and and_1 (x1, not_1_out, not_2_out, not_3_out);
  and and_2 (x2, p256, not_2_out, not_3_out);
  and and_3 (x3, p512, not_3_out);

  assign x4 = p768;
endmodule

module encoder (
  input  a,
  input  b,
  input  c,
  input  d,
  output [1:0] selct,
  output Enable
);

  wire and_1_out, and_2_out, and_3_out, and_4_out, and_5_out, and_6_out, and_7_out, and_8_out, not_1_out,
       not_2_out, not_3_out, not_4_out;

  not not_1 (not_1_out, a);
  not not_2 (not_2_out, b);
  not not_3 (not_3_out, c);
  not not_4 (not_4_out, d);
  and and_1 (and_1_out, not_4_out, c, not_2_out, not_1_out);
  and and_2 (and_2_out, d, not_3_out, not_2_out, not_1_out);
  and and_3 (and_3_out, not_4_out, not_3_out, b, not_1_out);
  and and_4 (and_4_out, d, not_3_out, not_2_out, not_1_out);
  and and_5 (and_5_out, not_4_out, not_3_out, not_2_out, a);
  and and_6 (and_6_out, not_4_out, not_3_out, b, not_1_out);
  and and_7 (and_7_out, not_4_out, c, not_2_out, not_1_out);
  and and_8 (and_8_out, d, not_3_out, not_2_out, not_1_out);
  or or_1 (selct[1], and_1_out, and_2_out);
  or or_2 (selct[0], and_3_out, and_4_out);
  or or_3 (Enable, and_5_out, and_6_out, and_7_out, and_8_out);
endmodule

module vgaCard (
  input  R,
  input  En,
  input  clock,
  input  nig,
  output [9:0] H,
  output [9:0] V
);

  wire vgatimig_1_pulse;
  wire [11:0] vgatimig_1_cod, vgatimig_2_cod;

  vgaTimig vgatimig_1 (
    .R(R), .En(En), .clock(clock), .resolution(12'h280), .BP(12'h10), .sync(12'h60), .FP(12'h30), .nig(nig),
    .cod(vgatimig_1_cod), .pulse(vgatimig_1_pulse));  // open: nxt
  vgaTimig vgatimig_2 (
    .R(R), .En(En), .clock(vgatimig_1_pulse), .resolution(12'h1e0), .BP(12'hb), .sync(12'h2), .FP(12'h21),
    .nig(nig), .cod(vgatimig_2_cod));  // open: nxt, pulse
  Bit_Extender #(.in_width(12), .out_width(10)) bit_extender_1 (.in(vgatimig_1_cod), .out(H));
  Bit_Extender #(.in_width(12), .out_width(10)) bit_extender_2 (.in(vgatimig_2_cod), .out(V));
endmodule

module vgaTimig (
  input  R,
  input  En,
  input  clock,
  input  [11:0] resolution,
  input  [11:0] BP,
  input  [11:0] sync,
  input  [11:0] FP,
  input  nig,
  output [11:0] cod,
  output nxt,
  output pulse
);

  wire and_2_out, comparator_1_eq, comparator_2_eq, comparator_3_eq, d_ff_1_q, or_1_out;
  wire [11:0] subtractor_1_out, subtractor_2_out, subtractor_3_out, subtractor_4_out;

  Subtractor #(.width(12)) subtractor_1 (.a(resolution), .b(12'h1), .out(subtractor_1_out));  // open: bin, bout
  Subtractor #(.width(12)) subtractor_2 (.a({12{1'b0}}), .b(BP), .out(subtractor_2_out));  // open: bin, bout
  Subtractor #(.width(12)) subtractor_3 (.a(subtractor_2_out), .b(sync), .out(subtractor_3_out));  // open: bin, bout
  Subtractor #(.width(12)) subtractor_4 (.a(subtractor_3_out), .b(FP), .out(subtractor_4_out));  // open: bin, bout
  Comparator #(.mode("unsigned"), .width(12)) comparator_1 (
    .a(cod), .b(subtractor_1_out), .eq(comparator_1_eq));  // open: gt, lt
  Comparator #(.mode("unsigned"), .width(12)) comparator_2 (
    .a(cod), .b(subtractor_2_out), .eq(comparator_2_eq));  // open: gt, lt
  Comparator #(.mode("unsigned"), .width(12)) comparator_3 (
    .a(cod), .b(subtractor_3_out), .eq(comparator_3_eq));  // open: gt, lt
  and and_1 (nxt, En, comparator_1_eq);
  or or_1 (or_1_out, comparator_3_eq, d_ff_1_q);
  and and_2 (and_2_out, ~comparator_2_eq, or_1_out);  // AND_Gate
  D_Flip_Flop d_ff_1 (.D(and_2_out), .clk(clock), .Q(d_ff_1_q), .reset(R));  // open: Qn, preset
  Counter #(.max('hfff), .width(12)) counter_1 (
    .clr(R), .load(nxt), .up(1'b1), .count(En), .clk(clock), .D(subtractor_4_out), .Q(cod));  // open: carry
  xor xor_1 (pulse, d_ff_1_q, nig);
endmodule
